# Fritzing sketch webserver-wifi (saved by Fritzing 0.9.9b)
breadboards: 1

parts:
  Part1 = Arduino Uno (Rev3) - ICSP
  U3 = ESP8266 WiFi Module [part_number=ESP8266]
  R1 = Resistor [tolerance=±5% resistance=1k package="0402 [SMD]"]
  S2 = Pushbutton [package="[THT]"]
  LED1 = smd LED [color="Red (633nm)" package="0805 [SMD]"]

nets:
  GND: Part1.GND, Part1.RESET, U3.GND, S2.Pin_1, S2.Pin_2, LED1.cathode
  N1: Part1.D0/RX, U3.RXD
  N2: Part1.D1/TX, U3.TXD
  3V3: Part1.3V3, U3.VCC, R1.Pin_0
  N3: U3.GPIO_0, S2.Pin_3, S2.Pin_4
  N4: U3.GPIO_2, LED1.anode
  N5: U3.CH_PD, R1.Pin_1

custom parts:
  ESP8266 WiFi Module: Generic WiFi Module based on the ESP8266 with onboard PCB antenna and UART communications
